# Fritzing sketch Aux PCB - Estación Meteorológica - IoT_v1.2.2 (saved by Fritzing 1.0.6)
circuit board: 8.2cm x 5.1cm
perfboards: 1

parts:
  J1_Inter-PCB = male pin header, 12 pins [form="♂ (male)"]
  JST1_Core_Sensors = female pin header, 4 pins [form="♀ (female)"]
  JST3_DHT11 = female pin header, 3 pins [form="♀ (female)"]
  JST4_Fot = female pin header, 3 pins [form="♀ (female)"]
  JST5_Veleta = female pin header, 5 pins [form="♀ (female)"]
  JST6_Temp_Sys = female pin header, 3 pins [form="♀ (female)"]
  JST7_Anem = female pin header, 3 pins [form="♀ (female)"]
  JST8_Pluv = female pin header, 3 pins [form="♀ (female)"]
  R2 = Resistor [tolerance=±5% power=0.25W resistance=10k package=THT]
  R3 = Resistor [tolerance=±5% power=0.25W resistance=10k package=THT]
  JST2_Rain_Sns = female pin header, 2 pins [form="♀ (female)"]
  C1 = Ceramic Capacitor [capacitance="100 nF" voltage=35V package="200 mil [THT, multilayer]"]
  Pad2 = Pad [width=7.874167894233263 height=2 connect=center]  # not connected
  Pad1 = Pad [width=2.6210023488006646 height=7.007260649562665 connect=center]  # not connected

nets:
  GND: J1_Inter-PCB.pin1, JST6_Temp_Sys.pin2, JST7_Anem.pin2, JST8_Pluv.pin2
  3.3V: J1_Inter-PCB.pin2, JST1_Core_Sensors.pin1, JST3_DHT11.pin1, JST4_Fot.pin1, JST5_Veleta.pin1, JST6_Temp_Sys.pin1, JST7_Anem.pin1, JST8_Pluv.pin1, R2.Pin_1, R3.Pin_1
  N1: J1_Inter-PCB.pin3, JST1_Core_Sensors.pin3, JST5_Veleta.pin3
  N2: J1_Inter-PCB.pin4, JST1_Core_Sensors.pin4, JST5_Veleta.pin4
  N3: J1_Inter-PCB.pin5, JST1_Core_Sensors.pin2
  N4: J1_Inter-PCB.pin6, JST3_DHT11.pin2, JST4_Fot.pin2, JST5_Veleta.pin2, JST2_Rain_Sns.pin1, C1.0
  N5: J1_Inter-PCB.pin7, JST7_Anem.pin3
  N6: J1_Inter-PCB.pin8, JST8_Pluv.pin3
  N7: J1_Inter-PCB.pin9, JST3_DHT11.pin3
  N8: J1_Inter-PCB.pin10, JST6_Temp_Sys.pin3
  N9: J1_Inter-PCB.pin11, JST4_Fot.pin3
  N10: J1_Inter-PCB.pin12, R2.Pin_0, R3.Pin_0, JST2_Rain_Sns.pin2, C1.1
