# Fritzing sketch Aux PCB - Estación Meteorológica - IoT_v1.2 (saved by Fritzing 1.0.6)
perfboards: 1

parts:
  J1 = male pin header, 12 pins [form="♂ (male)"]
  JST1_Core_Sensors = female pin header, 4 pins [form="♀ (female)"]
  JST2_Rain_Sens = female pin header, 3 pins [form="♀ (female)"]
  JST3_DHT11 = female pin header, 3 pins [form="♀ (female)"]
  JST4_Fotor = female pin header, 3 pins [form="♀ (female)"]
  JST5_Veleta = female pin header, 5 pins [form="♀ (female)"]
  JST6_Temp_Sys = female pin header, 3 pins [form="♀ (female)"]
  JST7_Anem = female pin header, 3 pins [form="♀ (female)"]
  JST8_Pluv = female pin header, 3 pins [form="♀ (female)"]

nets:
  GND: J1.pin1, JST6_Temp_Sys.pin2, JST7_Anem.pin2, JST8_Pluv.pin2
  3.3V: J1.pin2, JST1_Core_Sensors.pin1, JST2_Rain_Sens.pin1, JST3_DHT11.pin1, JST4_Fotor.pin1, JST5_Veleta.pin1, JST6_Temp_Sys.pin1, JST7_Anem.pin1, JST8_Pluv.pin1
  N1: J1.pin3, JST1_Core_Sensors.pin3, JST5_Veleta.pin3
  N2: J1.pin4, JST1_Core_Sensors.pin4, JST5_Veleta.pin4
  N3: J1.pin5, JST1_Core_Sensors.pin2
  N4: J1.pin6, JST2_Rain_Sens.pin2, JST3_DHT11.pin2, JST4_Fotor.pin2, JST5_Veleta.pin2
  N5: J1.pin7, JST7_Anem.pin3
  N6: J1.pin8, JST8_Pluv.pin3
  N7: J1.pin9, JST3_DHT11.pin3
  N8: J1.pin10, JST6_Temp_Sys.pin3
  N9: J1.pin11, JST4_Fotor.pin3
  N10: J1.pin12, JST2_Rain_Sens.pin3
