# Fritzing sketch Aux PCB - Estación Meteorológica - IoT_v1.3 (saved by Fritzing 1.0.6)
circuit board: 8.2cm x 5.1cm
perfboards: 1

parts:
  J1_Inter-PCB = male pin header, 12 pins [form="♂ (male)"]
  Core_Sensors = female pin header, 4 pins [form="♀ (female)"]
  DHT11 = female pin header, 3 pins [form="♀ (female)"]
  Foto = female pin header, 3 pins [form="♀ (female)"]
  Veleta = female pin header, 5 pins [form="♀ (female)"]
  Sys_Temp = female pin header, 3 pins [form="♀ (female)"]
  Anem = female pin header, 3 pins [form="♀ (female)"]
  Pluv = female pin header, 3 pins [form="♀ (female)"]
  R2 = Resistor [tolerance=±5% power=0.25W resistance=10k package=THT]
  R3 = Resistor [tolerance=±5% power=0.25W resistance=10k package=THT]
  Rain = female pin header, 2 pins [form="♀ (female)"]
  C1 = Ceramic Capacitor [capacitance="100 nF" voltage=35V package="200 mil [THT, multilayer]"]
  Pad2 = Pad [width=7.874167894233263 height=2 connect=center]  # not connected
  Pad1 = Pad [width=2.6210023488006646 height=7.007260649562665 connect=center]  # not connected

nets:
  GND: J1_Inter-PCB.pin1, Sys_Temp.pin2, Anem.pin2, Pluv.pin2
  3.3V: J1_Inter-PCB.pin2, Core_Sensors.pin1, DHT11.pin1, Foto.pin1, Veleta.pin1, Sys_Temp.pin1, Anem.pin1, Pluv.pin1, R2.Pin_1, R3.Pin_1
  N1: J1_Inter-PCB.pin3, Core_Sensors.pin3, Veleta.pin3
  N2: J1_Inter-PCB.pin4, Core_Sensors.pin4, Veleta.pin4
  N3: J1_Inter-PCB.pin5, Core_Sensors.pin2
  N4: J1_Inter-PCB.pin6, DHT11.pin2, Foto.pin2, Veleta.pin2, Rain.pin1, C1.0
  N5: J1_Inter-PCB.pin7, Anem.pin3
  N6: J1_Inter-PCB.pin8, Pluv.pin3
  N7: J1_Inter-PCB.pin9, DHT11.pin3
  N8: J1_Inter-PCB.pin10, Sys_Temp.pin3
  N9: J1_Inter-PCB.pin11, Foto.pin3
  N10: J1_Inter-PCB.pin12, R2.Pin_0, R3.Pin_0, Rain.pin2, C1.1
