# Fritzing sketch Main PCB - Estación Meteorológica - IoT_v1.5 (saved by Fritzing 1.0.6)
circuit board: 10.5cm x 8cm
circuit board: 1.28299cm x 2.23166cm
circuit board: 0.679082cm x 0.2cm
perfboards: 1

parts:
  ESP32_IZQ = female pin header, 8 pins [form="♀ (female)"]
  ESP32_DER = female pin header, 8 pins [form="♀ (female)"]
  J7_(Inter_PCB) = female pin header, 12 pins [form="♀ (female)"]
  INA_SYS = female pin header, 6 pins [form="♀ (female)"]
  INA_SOLAR = female pin header, 6 pins [form="♀ (female)"]
  R1_SCL = Resistor [tolerance=±5% power=0.25W resistance=2.2k package=THT]
  Q2_RAIL2 = NPN-Transistor [package="TO92 [THT]"]
  R3_RAIL1 = Resistor [tolerance=±5% power=0.25W resistance=2.2k package=THT]
  R4_RAIL2 = Resistor [tolerance=±5% power=0.25W resistance=2.2k package=THT]
  R5_PD_RAIL1 = Resistor [tolerance=±5% power=0.25W resistance=10k package=THT]
  R6_PD_RAIL2 = Resistor [tolerance=±5% power=0.25W resistance=10k package=THT]
  Q1_RAIL1 = NPN-Transistor [package="TO92 [THT]"]
  S-Up_VOUT = female pin header, 1 pin [form="♀ (female)"]
  Step-UP_GND1 = female pin header, 1 pin [form="♀ (female)"]
  Step-UP_VIN = female pin header, 1 pin [form="♀ (female)"]
  S-Up_GND2 = female pin header, 1 pin [form="♀ (female)"]
  CN3791 = female pin header, 4 pins [form="♀ (female)"]
  SOLAR = female pin header, 2 pins [form="♀ (female)"]
  R2_SDA = Resistor [tolerance=±5% power=0.25W resistance=2.2k package=THT]
  Pad1 = Pad [width=5 height=5 connect=center]  # not connected
  Pad2 = Pad [width=2 height=2 connect=center]  # not connected
  Pad3 = Pad [width=2 height=1 connect=center]  # not connected
  Pad4 = Pad [width=2 height=1 connect=center]  # not connected

nets:
  5V: ESP32_IZQ.pin1, S-Up_VOUT.pin1
  GND: ESP32_IZQ.pin2, J7_(Inter_PCB).pin1, INA_SYS.pin2, INA_SOLAR.pin2, Q2_RAIL2.E, R5_PD_RAIL1.Pin_0, R6_PD_RAIL2.Pin_0, Q1_RAIL1.E, Step-UP_GND1.pin1, S-Up_GND2.pin1, CN3791.pin2, CN3791.pin3, SOLAR.pin2
  3.3V: ESP32_IZQ.pin3, J7_(Inter_PCB).pin2, INA_SYS.pin1, INA_SOLAR.pin1, R1_SCL.Pin_0, R2_SDA.Pin_0
  N1: ESP32_IZQ.pin4, J7_(Inter_PCB).pin12
  N2: ESP32_IZQ.pin5, J7_(Inter_PCB).pin11
  N3: ESP32_IZQ.pin6, J7_(Inter_PCB).pin7
  N4: ESP32_IZQ.pin7, J7_(Inter_PCB).pin8
  N5: ESP32_IZQ.pin8, J7_(Inter_PCB).pin9
  N6: ESP32_DER.pin1, J7_(Inter_PCB).pin3, INA_SYS.pin3, INA_SOLAR.pin3, R1_SCL.Pin_1
  N7: ESP32_DER.pin2, J7_(Inter_PCB).pin4, INA_SYS.pin4, INA_SOLAR.pin4, R2_SDA.Pin_1
  N8: ESP32_DER.pin3, R3_RAIL1.Pin_0
  N9: ESP32_DER.pin4, R4_RAIL2.Pin_0
  N10: ESP32_DER.pin6, J7_(Inter_PCB).pin10
  N11: J7_(Inter_PCB).pin5, Q1_RAIL1.C
  N12: J7_(Inter_PCB).pin6, Q2_RAIL2.C
  N13: INA_SYS.pin5, Step-UP_VIN.pin1
  N14: INA_SYS.pin6, CN3791.pin4
  N15: INA_SOLAR.pin5, CN3791.pin1
  12V: INA_SOLAR.pin6, SOLAR.pin1
  N16: Q2_RAIL2.B, R4_RAIL2.Pin_1, R6_PD_RAIL2.Pin_1
  N17: R3_RAIL1.Pin_1, R5_PD_RAIL1.Pin_1, Q1_RAIL1.B

notes:
  VIN
  VOUT
  BAT
  CN3291
  VIN+
  VIN-
  SDA
  SCL
  GND
  VCC
  SIN
  SOLAR
  5V
  3.3
  GPIO2
  GPIO1
  GPIO0
  GPIO6
  GPIO7
  GPIO8
  GPIO5
  AN
  PL
  DS
  DHT
  FOT
  GPIO3
  GPIO4
  GPIO9
  GPIO10
  RN
  GPIO20
